# Fritzing sketch blinds server schematic (saved by Fritzing 0.9.2b)
breadboards: 2

parts:
  U1 = NodeMCU V1.0
  LED1 = LED - 5mm [color="Yellow (592nm)" package="5 mm [THT]"]
  LED2 = LED - 5mm [color="Green (565nm)" package="5 mm [THT]"]
  Part1 = Arduino Nano (Rev3.0)

nets:
  N1: U1.D4, LED2.anode
  N2: U1.GND, LED1.cathode, LED2.cathode
  N3: U1.D5, LED1.anode
  N4: U1.RX, Part1.D1/TX
  N5: U1.TX, Part1.D0/RX

custom parts:
  NodeMCU V1.0: ESP8266 based NodeMCU
