# Fritzing sketch blinds server shematic huzzah32 (saved by Fritzing 0.9.2b)
breadboards: 1

parts:
  Part1 = Adafruit HUZZAH32 ESP32 Feather [part_number="Adafruit #3405"]
  LED1 = LED - 5mm [color="Green (555nm)" package="5 mm [THT]"]
  LED2 = LED - 5mm [color="Yellow (585nm)" package="5 mm [THT]"]

nets:
  N1: Part1.GND, LED1.cathode, LED2.cathode
  N2: Part1.IO32_A7, LED2.anode
  N3: Part1.SCL, LED1.anode
